// Logisim project Lab01_Mux21.circ as structural Verilog: 1 circuit, main circuit main
module main (
  input  March_13__2024,
  input  in_2,
  input  in_3,
  output out_4
);

  wire and_1_out, and_2_out, not_1_out, not_2_out;

  not not_1 (not_1_out, March_13__2024);
  not not_2 (not_2_out, not_1_out);
  and and_1 (and_1_out, not_2_out, in_2);
  and and_2 (and_2_out, not_1_out, in_3);
  or or_1 (out_4, and_1_out, and_2_out);

  // Notes on the sheet:
  //   Moldir Azhimukhanbet
  //   Lab 01: 2-way, 1-Bit multiplexer
endmodule
