// Logisim project Lab04_ALU.circ as structural Verilog: 4 circuits, main circuit main
module main (
  input  CIn,
  input  [3:0] InA,
  input  [3:0] InB,
  input  [3:0] Sel,
  input  Mode,
  output COut,
  output Cmp,
  output [3:0] ALUOut
);

  ALU alu_1 (.CIn(CIn), .InA(InA), .InB(InB), .SeI(Sel), .Mode(Mode), .COut(COut), .Cmp(Cmp), .ALUOut(ALUOut));

  // Notes on the sheet:
  //   Lab 04: ALU
  //   March 14, 2024
  //   Moldir Azhimukhanbet
endmodule

module Arithmetic (
  input  Cin,
  input  [3:0] InA,
  input  [3:0] InB,
  input  [3:0] Sel,
  output [3:0] ArOut,
  output COut,
  output Cmp
);

  wire adder_1_cout, adder_2_cout, adder_3_cout, subtractor_1_bout, subtractor_2_bout, subtractor_3_bout,
       subtractor_4_bout, subtractor_5_bout;
  wire [3:0] adder_1_out, adder_2_out, adder_3_out, multiplier_2_out, not_1_out, not_2_out, not_3_out,
       or_1_out, subtractor_1_out, subtractor_2_out, subtractor_3_out, subtractor_4_out, subtractor_5_out;

  assign not_1_out = ~InB;  // NOT_Gate not_1, 4 bits wide
  Subtractor #(.width(4)) subtractor_1 (
    .a(InA), .b(4'b0001), .out(subtractor_1_out), .bin(Cin), .bout(subtractor_1_bout));
  Adder #(.width(4)) adder_1 (.a(InA), .b(InB), .out(adder_1_out), .cin(Cin), .cout(adder_1_cout));
  Subtractor #(.width(4)) subtractor_2 (.a(InA), .b(InB), .out(subtractor_2_out), .bin(Cin), .bout(subtractor_2_bout));
  Multiplier #(.width(4)) multiplier_1 (.a(InA), .b(InB));  // open: out, cin, cout
  Multiplier #(.width(4)) multiplier_2 (.a(InA), .b(not_1_out), .out(multiplier_2_out));  // open: cin, cout
  Adder #(.width(4)) adder_2 (.a(InA), .b(InA), .out(adder_2_out), .cin(Cin), .cout(adder_2_cout));
  Adder #(.width(4)) adder_3 (.a(InA), .b(4'b0001), .out(adder_3_out), .cin(Cin), .cout(adder_3_cout));
  Comparator #(.width(4)) comparator_1 (.a(InA), .b(InB), .eq(Cmp));  // open: gt, lt
  assign not_2_out = ~4'b0001;  // NOT_Gate not_2, 4 bits wide
  Subtractor #(.width(4)) subtractor_3 (.b(4'b0001), .out(subtractor_3_out), .bout(subtractor_3_bout));  // open: a, bin
  Subtractor #(.width(4)) subtractor_4 (
    .a(multiplier_2_out), .b(4'b0001), .out(subtractor_4_out), .bout(subtractor_4_bout));  // open: bin
  assign or_1_out = ~InB | InA;  // OR_Gate or_1, 4 bits wide
  Multiplexer #(.select(4)) multiplexer_1 (
    .in1(subtractor_5_bout), .in4(1'b0), .in5(subtractor_1_bout), .in6(adder_1_cout),
    .in7(subtractor_2_bout), .in9(subtractor_4_bout), .in10(adder_2_cout), .in11(adder_3_cout), .out(COut),
    .sel(Sel));  // open: in0, in2, in3, in8, in12, in13, in14, in15
  Multiplexer #(.select(4), .width(4)) multiplexer_2 (
    .in0(or_1_out), .in1(subtractor_5_out), .in4(not_2_out), .in5(subtractor_1_out), .in6(adder_1_out),
    .in7(subtractor_2_out), .in8(subtractor_3_out), .in9(subtractor_4_out), .in10(adder_2_out),
    .in11(adder_3_out), .out(ArOut), .sel(Sel));  // open: in2, in3, in12, in13, in14, in15
  Subtractor #(.width(4)) subtractor_5 (
    .a(InA), .b(not_3_out), .out(subtractor_5_out), .bin(Cin), .bout(subtractor_5_bout));
  assign not_3_out = ~InB;  // NOT_Gate not_3, 4 bits wide

  // Notes on the sheet:
  //   0=-1
  //   1=A-1
  //   2 = A + B
  //   3 = A - B
  //   4 = AB - 1
  //   5 = AB' - 1
  //   6 = A + A
  //   7 = A + 1
endmodule

module Logic (
  input  [3:0] InA,
  input  [3:0] InB,
  input  [2:0] Sel,
  output [3:0] LoOut
);

  wire [3:0] adder_1_out, adder_2_out, multiplier_1_out, multiplier_2_out, not_1_out, not_2_out, not_3_out,
       not_4_out, not_5_out, xor_1_out;

  assign not_1_out = ~InB;  // NOT_Gate not_1, 4 bits wide
  assign not_2_out = ~InB;  // NOT_Gate not_2, 4 bits wide
  assign not_3_out = ~InA;  // NOT_Gate not_3, 4 bits wide
  Multiplier #(.width(4)) multiplier_1 (.a(InA), .b(InB), .out(multiplier_1_out));  // open: cin, cout
  Adder #(.width(4)) adder_1 (.a(InB), .b(InA), .out(adder_1_out));  // open: cin, cout
  assign xor_1_out = InA ^ InB;  // XOR_Gate xor_1, 4 bits wide
  Multiplier #(.width(4)) multiplier_2 (.a(InA), .b(not_1_out), .out(multiplier_2_out));  // open: cin, cout
  Adder #(.width(4)) adder_2 (.a(InA), .b(not_2_out), .out(adder_2_out));  // open: cin, cout
  assign not_4_out = ~multiplier_1_out;  // NOT_Gate not_4, 4 bits wide
  assign not_5_out = ~adder_1_out;  // NOT_Gate not_5, 4 bits wide
  Multiplexer #(.select(3), .width(4)) multiplexer_1 (
    .in0(multiplier_1_out), .in1(not_4_out), .in2(adder_1_out), .in3(not_5_out), .in4(xor_1_out),
    .in5(multiplier_2_out), .in6(adder_2_out), .in7(not_3_out), .out(LoOut), .sel(Sel));
endmodule

module ALU (
  input  CIn,
  input  [3:0] InA,
  input  [3:0] InB,
  input  [3:0] SeI,
  input  Mode,
  output COut,
  output Cmp,
  output [3:0] ALUOut
);

  wire [2:0] undriven;
  wire [3:0] arithmetic_1_arout, logic_1_loout;

  Arithmetic arithmetic_1 (
    .Cin(CIn), .InA(InA), .InB(InB), .Sel(SeI), .ArOut(arithmetic_1_arout), .COut(COut), .Cmp(Cmp));
  Logic logic_1 (.InA(InA), .InB(InB), .Sel(undriven), .LoOut(logic_1_loout));
  Multiplexer #(.width(4)) multiplexer_1 (.in0(arithmetic_1_arout), .in1(logic_1_loout), .out(ALUOut), .sel(Mode));
endmodule
