// Logisim project Lab05_Vend.circ as structural Verilog: 6 circuits, main circuit main
module main (
  input  in_1
);

  Vending vending_1 (.Ena(in_1));  // open: In5, In10, In25, Vend01, Vend02, Vend03, Restock01, Restock02, Restock03, Rst, DepositeBCD, ChangeBCD, Prod01, Prod02, Prod03, Empty01, Empty02, Empty03, Dispense01, Dispense02, Dispense03
endmodule

module Vending (
  input  Ena,
  input  In5,
  input  In10,
  input  In25,
  input  Vend01,
  input  Vend02,
  input  Vend03,
  input  Restock01,
  input  Restock02,
  input  Restock03,
  input  Rst,
  output [11:0] DepositeBCD,
  output [11:0] ChangeBCD,
  output [7:0] Prod01,
  output [7:0] Prod02,
  output [7:0] Prod03,
  output Empty01,
  output Empty02,
  output Empty03,
  output Dispense01,
  output Dispense02,
  output Dispense03
);

  wire activator_1_activate;
  wire [7:0] bank_1_outacc;

  Bank bank_1 (.In5(In5), .In10(In10), .In25(In25), .Ena(Ena), .Rst(Rst), .OutAcc(bank_1_outacc));
  Activator activator_1 (
    .InCash(bank_1_outacc), .DepositedBCD(DepositeBCD), .ChangeBCD(ChangeBCD), .Activate(activator_1_activate));
  Dispenser dispenser_1 (
    .Activate(activator_1_activate), .Vend01(Vend01), .Vend02(Vend02), .Vend03(Vend03),
    .Restock01(Restock01), .Restock02(Restock02), .Restock03(Restock03), .Avail01(Prod01), .Avail02(Prod02),
    .Avail03(Prod03), .Empty01(Empty01), .Empty02(Empty02), .Empty03(Empty03), .Disp01(Dispense01),
    .Disp02(Dispense02), .Disp03(Dispense03));
endmodule

module Bank (
  input  In5,
  input  In10,
  input  In25,
  input  Ena,
  input  Rst,
  output [7:0] OutAcc
);

  wire or_1_out;
  wire [1:0] priority_encoder_1_out;
  wire [7:0] adder_1_out, multiplexer_1_out;

  or or_1 (or_1_out, In5, In10, In25);
  Priority_Encoder #(.select(2)) priority_encoder_1 (
    .in0(1'b1), .in1(In5), .in2(In10), .in3(In25), .out(priority_encoder_1_out), .en_in(Ena));  // open: gs, en_out
  Multiplexer #(.select(2), .width(8)) multiplexer_1 (
    .in0({8{1'b0}}), .in1(8'h5), .in2(8'ha), .in3(8'h19), .out(multiplexer_1_out),
    .sel(priority_encoder_1_out));
  Register register_1 (.D(adder_1_out), .en(Ena), .clk(or_1_out), .Q(OutAcc), .clr(Rst));
  Adder adder_1 (.a(OutAcc), .b(multiplexer_1_out), .out(adder_1_out));  // open: cin, cout
endmodule

module Dispenser (
  input  Activate,
  input  Vend01,
  input  Vend02,
  input  Vend03,
  input  Restock01,
  input  Restock02,
  input  Restock03,
  output [7:0] Avail01,
  output [7:0] Avail02,
  output [7:0] Avail03,
  output Empty01,
  output Empty02,
  output Empty03,
  output Disp01,
  output Disp02,
  output Disp03
);

  wire demultiplexer_1_out1, demultiplexer_1_out2, demultiplexer_1_out3;
  wire [1:0] priority_encoder_1_out;

  Demultiplexer #(.select(2)) demultiplexer_1 (
    .out1(demultiplexer_1_out1), .out2(demultiplexer_1_out2), .out3(demultiplexer_1_out3), .in(Activate),
    .sel(priority_encoder_1_out));  // open: out0
  Priority_Encoder #(.select(2)) priority_encoder_1 (
    .in0(1'b1), .in1(Vend01), .in2(Vend02), .in3(Vend03), .out(priority_encoder_1_out), .en_in(1'b1));  // open: gs, en_out
  Product product_1 (
    .Restock(Restock01), .Vend(demultiplexer_1_out1), .Avail_BCD(Avail01), .Empty(Empty01), .Dispensed(Disp01));
  Product product_2 (
    .Restock(Restock02), .Vend(demultiplexer_1_out2), .Avail_BCD(Avail02), .Empty(Empty02), .Dispensed(Disp02));
  Product product_3 (
    .Restock(Restock03), .Vend(demultiplexer_1_out3), .Avail_BCD(Avail03), .Empty(Empty03), .Dispensed(Disp03));
endmodule

module Product (
  input  Restock,
  input  Vend,
  output [7:0] Avail_BCD,
  output Empty,
  output Dispensed
);

  wire not_1_out, or_1_out;
  wire [3:0] counter_1_q;

  or or_1 (or_1_out, Restock, Vend);
  not not_1 (not_1_out, Empty);
  and and_1 (Dispensed, ~Empty, Vend);  // AND_Gate
  Counter #(.max('hf), .width(4)) counter_1 (
    .load(Restock), .up(1'b0), .count(not_1_out), .clk(or_1_out), .D(4'b1111), .carry(Empty), .Q(counter_1_q));  // open: clr
  // Binary_to_BCD_converter #(.binvalue(4)) binary_to_bcd_converter_1: pin names not known; wires that end beside it: counter_1_q, Avail_BCD[7:4], Avail_BCD[3:0]
endmodule

module Activator (
  input  [7:0] InCash,
  output [11:0] DepositedBCD,
  output [11:0] ChangeBCD,
  output Activate
);

  wire comparator_1_eq, comparator_1_gt;
  wire [7:0] multiplexer_1_out, subtractor_1_out;

  // Binary_to_BCD_converter #(.binvalue(8)) binary_to_bcd_converter_1: pin names not known; wires that end beside it: InCash, DepositedBCD[11:8], DepositedBCD[7:4], DepositedBCD[3:0]
  Comparator comparator_1 (.a(InCash), .b(8'h4b), .gt(comparator_1_gt), .eq(comparator_1_eq));  // open: lt
  Multiplexer #(.width(8)) multiplexer_1 (.in0(8'h4b), .in1(InCash), .out(multiplexer_1_out), .sel(comparator_1_gt));
  or or_1 (Activate, comparator_1_gt, comparator_1_eq);
  Subtractor subtractor_1 (.a(multiplexer_1_out), .b(8'h4b), .out(subtractor_1_out));  // open: bin, bout
  // Binary_to_BCD_converter #(.binvalue(8)) binary_to_bcd_converter_2: pin names not known; wires that end beside it: multiplexer_1_out, subtractor_1_out, ChangeBCD[11:8], ChangeBCD[7:4], ChangeBCD[3:0]
endmodule
